# Fritzing sketch design-max30205 (saved by Fritzing 0.9.6b)
breadboards: 1

parts:
  Mod1 = Raspberry Pi 4B
  R1 = Resistor [tolerance=±5% power=0.25 resistance=4.7k package=THT]
  C1 = Electrolytic Capacitor [capacitance=1μF voltage=35V package="0405 [SMD, electrolytic]"]  # not connected
  M1 = Max30205 body temp sensor [package=THT]  # not connected
  R2 = Resistor [tolerance=±5% power=0.25 resistance=4.7k package=THT]
  R3 = Resistor [tolerance=±5% power=0.25 resistance=4.7k package=THT]

nets:
  N1: Mod1.3V3, R1.Pin_0, R2.Pin_0, R3.Pin_1
  N2: Mod1.GPIO2, R1.Pin_1
  N3: Mod1.GPIO3, R2.Pin_1

custom parts:
  Max30205 body temp sensor: This module is based on MAX30205 which is a temperature sensor that accurately measures temperature and provides an over-temperature alarm/interrupt/shutdown output.
