# Fritzing sketch design-dht22 (saved by Fritzing 0.9.6b)
breadboards: 1

parts:
  Mod1 = Raspberry Pi 4B
  RHT2 = Humidity and Temperature Sensor RHT03
  R2 = Resistor [tolerance=±5% resistance=10k package="0603 [SMD]"]

nets:
  3V3: Mod1.3V3, RHT2.Vcc, R2.Pin_0
  N1: Mod1.GND, RHT2.GND_2
  N2: Mod1.GPIO17, RHT2.Data-signal, R2.Pin_1
